// Logisim project 2Bit_ALU.circ as structural Verilog: 1 circuit, main circuit main
module main (
  input  in_1,
  input  in_2,
  input  in_3,
  input  in_4,
  input  [1:0] in_5,
  input  in_6,
  input  in_7,
  output out_8,
  output out_9
);

  wire and_1_out, and_2_out, not_1_out, not_2_out, or_1_out, or_2_out, xor_1_out, xor_2_out;

  and and_1 (and_1_out, in_1, in_3);
  or or_1 (or_1_out, in_1, in_3);
  xor xor_1 (xor_1_out, in_1, in_3);
  not not_1 (not_1_out, in_1);
  Multiplexer #(.select(2)) multiplexer_1 (
    .in0(and_1_out), .in1(or_1_out), .in2(xor_1_out), .in3(not_1_out), .out(out_9), .sel(in_5), .en(in_6));
  and and_2 (and_2_out, in_2, in_4);
  or or_2 (or_2_out, in_2, in_4);
  xor xor_2 (xor_2_out, in_2, in_4);
  not not_2 (not_2_out, in_2);
  Multiplexer #(.select(2)) multiplexer_2 (
    .in0(and_2_out), .in1(or_2_out), .in2(xor_2_out), .in3(not_2_out), .out(out_8), .sel(in_5), .en(in_7));
endmodule
