// Logisim project 3to8 Decoder.circ as structural Verilog
module _3to8_Decoder (
  input  I2,
  input  I1,
  input  I0,
  output D0,
  output D1,
  output D2,
  output D3,
  output D4,
  output D5,
  output D6,
  output D7
);

  wire not_1_out, not_2_out, not_3_out, not_4_out, not_5_out, not_6_out, not_7_out, not_8_out, not_9_out,
       not_10_out, not_11_out, not_12_out;

  not not_1 (not_1_out, I2);
  not not_2 (not_2_out, I1);
  not not_3 (not_3_out, I0);
  not not_4 (not_4_out, I2);
  not not_5 (not_5_out, I1);
  not not_6 (not_6_out, I2);
  not not_7 (not_7_out, I0);
  not not_8 (not_8_out, I2);
  not not_9 (not_9_out, I1);
  not not_10 (not_10_out, I0);
  not not_11 (not_11_out, I1);
  not not_12 (not_12_out, I0);
  and and_1 (D7, I2, I1, I0);
  and and_2 (D0, not_1_out, not_2_out, not_3_out);
  and and_3 (D1, not_4_out, not_5_out, I0);
  and and_4 (D2, not_6_out, I1, not_7_out);
  and and_5 (D3, not_8_out, I1, I0);
  and and_6 (D4, I2, not_9_out, not_10_out);
  and and_7 (D5, I2, not_11_out, I0);
  and and_8 (D6, I2, I1, not_12_out);
endmodule
