// Logisim project Adder_Subtractor.circ as structural Verilog: 1 circuit, main circuit main
module main (
  input  in_1,
  input  in_2,
  input  in_3,
  input  in_4,
  input  in_5,
  input  in_6,
  input  in_7,
  input  in_8,
  input  in_9,
  input  in_10,
  input  in_11,
  input  in_12,
  input  in_13,
  input  in_14,
  input  in_15,
  input  in_16,
  input  in_17,
  input  in_18,
  output out_19,
  output out_20,
  output out_21,
  output out_22,
  output out_23,
  output out_24,
  output out_25,
  output out_26,
  output out_27,
  output out_28
);

  wire adder_1_cout, adder_2_cout, adder_3_cout, adder_5_cout, adder_6_cout, adder_7_cout, xor_1_out,
       xor_2_out, xor_3_out, xor_4_out;

  Adder #(.width(1)) adder_1 (.a(in_3), .b(in_5), .out(out_19), .cin(in_1), .cout(adder_1_cout));
  Adder #(.width(1)) adder_2 (.a(in_7), .b(in_9), .out(out_21), .cin(adder_1_cout), .cout(adder_2_cout));
  Adder #(.width(1)) adder_3 (.a(in_11), .b(in_13), .out(out_23), .cin(adder_2_cout), .cout(adder_3_cout));
  Adder #(.width(1)) adder_4 (.a(in_15), .b(in_17), .out(out_25), .cin(adder_3_cout), .cout(out_27));
  xor xor_1 (xor_1_out, in_6, in_2);
  xor xor_2 (xor_2_out, in_10, in_2);
  xor xor_3 (xor_3_out, in_14, in_2);
  xor xor_4 (xor_4_out, in_18, in_2);
  Adder #(.width(1)) adder_5 (.a(in_4), .b(xor_1_out), .out(out_20), .cin(in_2), .cout(adder_5_cout));
  Adder #(.width(1)) adder_6 (.a(in_8), .b(xor_2_out), .out(out_22), .cin(adder_5_cout), .cout(adder_6_cout));
  Adder #(.width(1)) adder_7 (.a(in_12), .b(xor_3_out), .out(out_24), .cin(adder_6_cout), .cout(adder_7_cout));
  Adder #(.width(1)) adder_8 (.a(in_16), .b(xor_4_out), .out(out_26), .cin(adder_7_cout), .cout(out_28));
endmodule
