// Logisim project Demux4x1.circ as structural Verilog: 1 circuit, main circuit main
module main (
  input  S1,
  input  S0,
  input  Input,
  output D0,
  output D1,
  output D2,
  output D3
);

  wire not_1_out, not_2_out;

  not not_1 (not_1_out, S1);
  not not_2 (not_2_out, S0);
  and and_1 (D0, Input, not_2_out, not_1_out);
  and and_2 (D1, Input, S0, not_1_out);
  and and_3 (D2, Input, S1, not_2_out);
  and and_4 (D3, Input, S0, S1);

  // Notes on the sheet:
  //   ......................Selection Lines...................
endmodule
