// Logisim project Demux8x1.circ as structural Verilog: 1 circuit, main circuit main
module main (
  input  in_1,
  input  in_2,
  input  S0,
  input  in_4,
  output D0,
  output D1,
  output D2,
  output D3,
  output D4,
  output D5,
  output D6,
  output D7
);

  wire not_1_out, not_2_out, not_3_out;

  not not_1 (not_1_out, in_1);
  not not_2 (not_2_out, in_2);
  not not_3 (not_3_out, S0);
  and and_1 (D0, in_4, not_3_out, not_2_out, not_1_out);
  and and_2 (D1, in_4, S0, not_2_out, not_1_out);
  and and_3 (D2, in_4, not_3_out, in_2, not_1_out);
  and and_4 (D3, in_4, S0, in_2, not_1_out);
  and and_5 (D4, in_4, not_3_out, not_2_out, in_1);
  and and_6 (D5, in_4, S0, not_2_out, in_1);
  and and_7 (D6, in_4, not_3_out, in_2, in_1);
  and and_8 (D7, in_4, S0, in_2, in_1);

  // Notes on the sheet:
  //   S2
  //   S1
  //   INPUT VALUE
endmodule
