// Logisim project Mux4x1.circ as structural Verilog: 1 circuit, main circuit main
module main (
  input  in_1,
  input  in_2,
  input  D0,
  input  D1,
  input  D2,
  input  D3,
  output out_7
);

  wire and_1_out, and_2_out, and_3_out, and_4_out, not_1_out, not_2_out;

  not not_1 (not_1_out, in_1);
  not not_2 (not_2_out, in_2);
  and and_1 (and_1_out, D0, not_2_out, not_1_out);
  and and_2 (and_2_out, D1, in_2, not_1_out);
  and and_3 (and_3_out, D2, not_2_out, in_1);
  and and_4 (and_4_out, D3, in_2, in_1);
  or or_1 (out_7, and_1_out, and_2_out, and_3_out, and_4_out);

  // Notes on the sheet:
  //   S1                               S0
endmodule
